# Fritzing sketch Untitled Sketch 3 (saved by Fritzing 0.9.3b)

parts:
  元件1 = Arduino Uno (Rev3) - ICSP
  元件2 = Arduino Pro Mini (5V)

nets:
  5V: 元件1.5V, 元件2.VCC
  GND: 元件1.GND, 元件2.GND
  N1: 元件1.D0/RX, 元件2.TXO
  N2: 元件1.D1/TX, 元件2.RXI
