# Fritzing sketch relay (saved by Fritzing 0.9.3b)
breadboards: 1

parts:
  元件1 = Arduino Uno (Rev3)
  U1 = G3VM-61E1 [package=g3vm-61e1]
  LED1 = LED - 5mm [color="Red (633nm)" package="5 mm [THT]"]
  LED2 = LED - 5mm [color="Red (633nm)" package="5 mm [THT]"]

nets:
  N1: 元件1.D8, U1.P$1
  N2: 元件1.GND, U1.P$3
  N3: 元件1.3V3, U1.P$2
  N4: 元件1.5V, U1.P$5
  N5: U1.P$4, LED1.anode
  N6: U1.P$6, LED2.anode
  N7: LED1.cathode, LED2.cathode
